# Fritzing sketch Esquema montaje CDI (saved by Fritzing 0.9.3b)
breadboards: 1

parts:
  Q1 = SCR-X0405MF - BUENO [package="to600v 4a"]
  Componente1 = Arduino Uno (Rev3) - ICSP
  LED1 = smd LED [color="Red (633nm)" package="1206 [SMD]"]
  R1 = Resistor [tolerance=±5% resistance=220 package=THT]
  U1 = BUTTON-MAGNETIC [package=Magnetic-snap]

nets:
  N1: Q1.Gate, Componente1.D9_PWM
  N2: Q1.Source, LED1.anode
  N3: Componente1.A0, U1.1
  N4: LED1.cathode, R1.Pin_1

notes:
  <= 12v
  de la motocicleta
  Sensor PickUp
  motocicleta=>
  -LED (para estroboscopico)
  o
  -Bobina de Descarga (CDI)
  *(Puede usarse MOSFET N)
  <=SRC X0405MF

custom parts:
  SCR-X0405MF - BUENO: SUCEDANEO DE TIRISTOR SCR X0405MF
