# Fritzing sketch Invernadero Plano (saved by Fritzing 0.9.3b)
breadboards: 1

parts:
  Componente1 = Arduino Uno (Rev3) - ICSP
  Componente2 = FC-28 Soil Hygrometer Module - Probe
  Componente3 = FC-28 Soil Hygrometer Module
  Componente4 = FC-28 Soil Hygrometer Module - Probe
  Componente5 = FC-28 Soil Hygrometer Module
  J1 = Generic male header - 3 pins [form="♂ (male)" package=THT]
  Nokia_5110_LCD_Module1 = Nokia 5110 LCD
  U1 = 4RelayModule
  ZS-042_RTC1 = ZS-042 RTC Module
  U2 = 2RelayModule
  Part1 = KY-006 Passive Buzzer Module [package="Breakout board"]
  R1 = Trimmer Potentiometer [maximum_resistance=550Ω package=THT]
  R2 = Resistor [tolerance=±5% resistance=100 package=THT]
  R3 = Resistor [tolerance=±5% resistance=200 package=THT]
  YwRobot_Power_Supply1 = YwRobot Breadboard Power Supply [part_number=545043]

nets:
  N1: Componente1.A1, Componente3.AO
  N2: Componente1.A2, Componente5.AO
  N3: Componente1.A3, J1.pin3
  N4: Componente1.A4/SDA, ZS-042_RTC1.SDA
  N5: Componente1.A5/SCL, ZS-042_RTC1.SCL
  N6: Componente1.ICSP_MOSI, Componente1.D11_PWM/MOSI, U2.IN2
  N7: Componente1.D8, U1.IN3
  N8: Componente1.D9_PWM, U1.IN2
  N9: Componente1.D10_PWM/SS, U1.IN1
  N10: Componente1.D12/MISO, U2.IN1
  N11: Componente1.D13/SCK, Part1.S
  N12: Componente1.D2, U1.IN4
  N13: Componente1.D3_PWM, Nokia_5110_LCD_Module1.SCLK
  N14: Componente1.D4, Nokia_5110_LCD_Module1.DN(MOSI)
  N15: Componente1.D5_PWM, Nokia_5110_LCD_Module1.D/C
  N16: Componente1.D6_PWM, Nokia_5110_LCD_Module1.RST
  N17: Componente1.D7, Nokia_5110_LCD_Module1.SCE
  N18: Componente2.POS, Componente5.POS
  N19: Componente2.NEG, Componente5.NEG
  VCC: Componente3.VCC, Componente5.VCC, J1.pin1, J1.pin2, ZS-042_RTC1.VCC, YwRobot_Power_Supply1.VCC#5
  GND: Componente3.GND, Componente5.GND, ZS-042_RTC1.GND, R3.Pin_0, YwRobot_Power_Supply1.GND#11
  N20: Componente3.POS, Componente4.POS
  N21: Componente3.NEG, Componente4.NEG
  N22: Nokia_5110_LCD_Module1.VCC_(out), R2.Pin_1, R3.Pin_1
  N23: Nokia_5110_LCD_Module1.GND_(out), R1.leg2
  N24: Nokia_5110_LCD_Module1.LED_(out), R1.leg1
  GND_2: U1.GND, U2.GND, Part1.-, R1.wiper, YwRobot_Power_Supply1.GND#13
  VCC_2: U1.VCC, U2.VCC, R2.Pin_0, YwRobot_Power_Supply1.VCC#9

custom parts:
  FC-28 Soil Hygrometer Module - Probe: The FC-28 is a soil hygrometer module that uses the Texas Instruments LM393 comparator chip to provide an analog measurement of soil humidity.
  FC-28 Soil Hygrometer Module: The FC-28 is a soil hygrometer module that uses the Texas Instruments LM393 comparator chip to provide an analog measurement of soil humidity. The digital output is high when soil moisture is over a certain threshold, as determined by adjusting the potentiometer.
  Generic male header - 3 pins: Generic male header
  Nokia 5110 LCD: Nokia 5110 Graphic 84*48 LCD module such as the Sparkfun LCD-10168 or the clones from Ebay. There is example code for the Arduino available from the Sparkfun site in https://learn.sparkfun.com/tutorials/graphic-lcd-hookup-guide This is a 3.3V device, if you are running it from a 5V micro you need a 5V tolorant level translator such as the 74ahc367 to protect the signal imputs. Rafa G. did a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
  4RelayModule: 4 relay arduino module SONGLE SRD05VDC-SL-C
  2RelayModule: 2 relay arduino module SONGLE SRD05VDC-SL-C
  KY-006 Passive Buzzer Module: Passive Piezoelectric Buzzer Module Keyes KY-006, it can produce a range of sound tones depending on the input frequency.
  YwRobot Breadboard Power Supply: The YwRobot Breadboard Power Supply (MB-V2) has two power rails; they can be 5V or 3V3. Power to the module can be provided through the female USB socket or through the A10 (female) 2.1mm power jack.
